# Fritzing sketch I2C_pcf8574 (saved by Fritzing 0.9.3b)
stripboards: 1

parts:
  U1 = PCF8574 [package="DIP16 [THT]"]
  J1 = Screw terminal - 2 pins [package=THT]
  J2 = Screw terminal - 2 pins [package=THT]
  R2 = Resistor [tolerance=±5% resistance=10k package=THT]
  R1 = Resistor [tolerance=±5% resistance=10k package=THT]
  J3 = female pin header, 3 pins [form="♀ (female)"]
  J4 = female pin header, 3 pins [form="♀ (female)"]
  R3 = Resistor [tolerance=±5% resistance=10k package=THT]
  R4 = Resistor [tolerance=±5% resistance=10k package=THT]
  R5 = Resistor [tolerance=±5% resistance=10k package=THT]
  J5 = female pin header, 8 pins [form="♀ (female)"]
  U2 = PCF8574 [package="DIP16 [THT]"]
  J6 = female pin header, 3 pins [form="♀ (female)"]
  R6 = Resistor [tolerance=±5% resistance=10k package=THT]
  R7 = Resistor [tolerance=±5% resistance=10k package=THT]
  R8 = Resistor [tolerance=±5% resistance=10k package=THT]
  R9 = Resistor [tolerance=±5% resistance=10k package=THT]
  R10 = Resistor [tolerance=±5% resistance=10k package=THT]
  J7 = screw terminal, 8 pins  # not connected
  J8 = screw terminal, 8 pins
  R11 = Resistor [tolerance=±5% resistance=10k package=THT]
  J9 = female pin header, 8 pins [form="♀ (female)"]
  R12 = Resistor [tolerance=±5% resistance=10k package=THT]
  J10 = female pin header, 8 pins [form="♀ (female)"]
  R13 = Resistor [tolerance=±5% resistance=10k package=THT]
  R14 = Resistor [tolerance=±5% resistance=10k package=THT]

nets:
  N1: U1.A0, J4.pin1, R3.Pin_0
  N2: U1.A1, J4.pin2, R4.Pin_0
  N3: U1.A3, J4.pin3, R5.Pin_0
  N4: U1.P0, J5.pin1
  N5: U1.P1, J5.pin2
  N6: U1.P2, J5.pin3
  N7: U1.P3, J5.pin4
  GND: U1.GND, J1.pin2, J3.pin1, J3.pin2, J3.pin3, U2.GND, J6.pin1, J6.pin2, J6.pin3, R11.Pin_1, R12.Pin_1, R13.Pin_1, R14.Pin_1
  N8: U1.P4, J5.pin8
  N9: U1.P5, J5.pin7
  N10: U1.P6, J5.pin6
  N11: U1.P7, J5.pin5
  N12: U1.SCL, J2.pin2, R2.Pin_0
  N13: U1.SDA, J2.pin1, R1.Pin_0
  VCC: U1.VCC, J1.pin1, R2.Pin_1, R1.Pin_1, R3.Pin_1, R4.Pin_1, R5.Pin_1, U2.VCC, R6.Pin_0, R7.Pin_0, R8.Pin_0, R9.Pin_0, R10.Pin_0, J8.pin1, J8.pin2, J8.pin3, J8.pin4, J8.pin5, J8.pin6, J8.pin7, J8.pin8
  N14: U2.A0, R8.Pin_1
  N15: U2.A1, R9.Pin_1
  N16: U2.A3, R10.Pin_1
  N17: U2.P0, R11.Pin_0, J9.pin8, J10.pin8
  N18: U2.P1, J9.pin7, R12.Pin_0, J10.pin7
  N19: U2.P2, U2.P5, J9.pin3, J9.pin6, J10.pin3, J10.pin6, R13.Pin_0
  N20: U2.P3, J9.pin5, J10.pin5, R14.Pin_0
  N21: U2.P4, J9.pin4, J10.pin4
  N22: U2.P6, J9.pin2, J10.pin2
  N23: U2.P7, J9.pin1, J10.pin1
  N24: U2.SCL, R7.Pin_1
  N25: U2.SDA, R6.Pin_1

notes:
  SDA SCL
  5V GND
  Key Pin 1
