# Fritzing sketch baseBoard1284_new (saved by Fritzing 0.9.3b)
stripboards: 1

parts:
  R6 = Resistor [tolerance=±5% resistance=10k package=THT]
  S2 = Pushbutton [package="[THT]"]
  R7 = Resistor [tolerance=±5% resistance=220 package=THT]
  R8 = Resistor [tolerance=±5% resistance=220 package=THT]
  C6 = Ceramic Capacitor [capacitance=100nF package="100 mil [THT, multilayer]"]
  C7 = Ceramic Capacitor [capacitance=100nF package="100 mil [THT, multilayer]"]
  XTAL2 = Crystal [frequency="16 Mhz" package=THT]
  C8 = Ceramic Capacitor [capacitance=22pF package="100 mil [THT, multilayer]"]
  C9 = Ceramic Capacitor [capacitance=22pF package="100 mil [THT, multilayer]"]
  J3 = Screw terminal - 2 pins [package=THT]
  J4 = Screw terminal - 2 pins [package=THT]
  J_FTDI1 = female pin header, 5 pins [form="♀ (female)"]
  J5 = Screw terminal - 2 pins [package=THT]
  C10 = Ceramic Capacitor [capacitance=100nF package="100 mil [THT, multilayer]"]
  Q2 = NPN-Transistor [package="TO92 [THT]"]
  R10 = Resistor [tolerance=±5% resistance=220 package=THT]
  JRelay = female pin header, 3 pins [form="♀ (female)"]
  J_SPK1 = female pin header, 2 pins [form="♀ (female)"]
  R11 = Resistor [tolerance=±5% resistance=220 package=THT]
  JLED = female pin header, 5 pins [form="♀ (female)"]
  R12 = Resistor [tolerance=±5% resistance=10k package=THT]
  R13 = Resistor [tolerance=±5% resistance=10k package=THT]
  JLCD = female pin header, 4 pins [form="♀ (female)"]
  R14 = Resistor [tolerance=±5% resistance=10k package=THT]
  R15 = Resistor [tolerance=±5% resistance=10k package=THT]
  R16 = Resistor [tolerance=±5% resistance=10k package=THT]
  J8 = female pin header, 3 pins [form="♀ (female)"]
  J9 = female pin header, 3 pins [form="♀ (female)"]
  JKeyPad = female pin header, 8 pins [form="♀ (female)"]
  J11 = screw terminal, 8 pins  # not connected
  Atmega1 = ATmega644 [package=pdpi]
  U1 = PCF8574 [package="DIP16 [THT]"]
  R17 = Resistor [tolerance=±5% resistance=220 package=THT]
  R18 = Resistor [tolerance=±5% resistance=220 package=THT]
  LED1 = LED - 3mm [color="Red (633nm)" package="3 mm [THT]"]

nets:
  N1: R6.Pin_0, C10.0, Atmega1.RESET
  VCC: R6.Pin_1, C6.1, C7.0, J4.pin1, J_FTDI1.pin2, J5.pin2, Q2.C, JRelay.pin1, R12.Pin_1, R13.Pin_1, JLCD.pin1, R14.Pin_1, R15.Pin_1, R16.Pin_1, Atmega1.VCC, Atmega1.AVCC, Atmega1.AREF, U1.VCC, R18.Pin_0
  GND: S2.Pin_1, S2.Pin_2, C6.0, C7.1, C8.1, C9.1, J4.pin2, J_FTDI1.pin1, J5.pin1, JRelay.pin2, J_SPK1.pin1, JLED.pin1, JLCD.pin2, J8.pin1, J8.pin2, J8.pin3, Atmega1.GND, U1.GND, LED1.cathode
  N2: S2.Pin_3, S2.Pin_4, Atmega1.PB7
  N3: R7.Pin_0, Atmega1.PB1
  N4: R7.Pin_1, JLED.pin2
  N5: R8.Pin_0, Atmega1.PB2
  N6: R8.Pin_1, JLED.pin3
  N7: XTAL2.pin_0, C9.0, Atmega1.XTAL1
  N8: XTAL2.pin_1, C8.0, Atmega1.XTAL2
  N9: J3.pin1, R13.Pin_0, JLCD.pin4, Atmega1.PC0, U1.SCL
  N10: J3.pin2, R12.Pin_0, JLCD.pin3, Atmega1.PC1, U1.SDA
  N11: J_FTDI1.pin3, Atmega1.PD0
  N12: J_FTDI1.pin4, Atmega1.PD1
  N13: J_FTDI1.pin5, C10.1
  N14: Q2.E, J_SPK1.pin2
  N15: Q2.B, R10.Pin_1
  N16: R10.Pin_0, Atmega1.PD5
  N17: JRelay.pin3, Atmega1.PD6
  N18: R11.Pin_0, Atmega1.PB4
  N19: R11.Pin_1, JLED.pin5
  N20: JLED.pin4, R17.Pin_1
  N21: R14.Pin_0, J9.pin1, U1.A3
  N22: R15.Pin_0, J9.pin2, U1.A1
  N23: R16.Pin_0, J9.pin3, U1.A0
  N24: JKeyPad.pin1, U1.P4
  N25: JKeyPad.pin2, U1.P5
  N26: JKeyPad.pin3, U1.P6
  N27: JKeyPad.pin4, U1.P7
  N28: JKeyPad.pin5, U1.P3
  N29: JKeyPad.pin6, U1.P2
  N30: JKeyPad.pin7, U1.P1
  N31: JKeyPad.pin8, U1.P0
  N32: Atmega1.PB3, R17.Pin_0
  N33: R18.Pin_1, LED1.anode

notes:
  SCL
  SDA
  Relay
  Spk
  LedAttivato
  LedDisattivo
  LedAnomalie
  LedMonSirena
  LCD
